// Logisim project 19-bit.circ as structural Verilog: 25 circuits, main circuit main
module main (
  input  [18:0] IR,
  input  [15:0] Seq,
  input  R,
  input  I0,
  input  I1,
  output S0,
  output S1,
  output S2
);

  wire and_1_out, and_2_out, and_3_out, and_4_out, and_5_out, and_6_out, and_7_out, and_8_out, and_9_out,
       and_10_out, and_11_out, and_12_out, and_13_out, and_14_out, and_15_out, and_16_out, and_17_out,
       and_18_out, and_19_out, and_20_out, and_21_out, and_22_out, and_23_out, and_24_out, decoder_1_out0,
       decoder_1_out1, decoder_1_out2, decoder_1_out3, decoder_1_out4, decoder_1_out5, decoder_1_out6,
       decoder_1_out7, decoder_1_out8, decoder_1_out9, decoder_1_out10, decoder_1_out11, decoder_1_out12,
       decoder_1_out13, decoder_1_out14, decoder_1_out15, or_1_out, or_2_out, or_3_out, or_4_out, or_5_out,
       or_6_out;

  Decoder #(.select(4)) decoder_1 (
    .out0(decoder_1_out0), .out1(decoder_1_out1), .out2(decoder_1_out2), .out3(decoder_1_out3),
    .out4(decoder_1_out4), .out5(decoder_1_out5), .out6(decoder_1_out6), .out7(decoder_1_out7),
    .out8(decoder_1_out8), .out9(decoder_1_out9), .out10(decoder_1_out10), .out11(decoder_1_out11),
    .out12(decoder_1_out12), .out13(decoder_1_out13), .out14(decoder_1_out14), .out15(decoder_1_out15),
    .sel(IR[16:13]));  // open: en
  and and_1 (and_1_out, decoder_1_out15, Seq[3], I0, I1);
  and and_2 (and_2_out, decoder_1_out10, Seq[6]);
  and and_3 (and_3_out, Seq[5], decoder_1_out11);
  and and_4 (and_4_out, ~decoder_1_out15, Seq[3], I0, ~I1);  // AND_Gate
  and and_5 (and_5_out, ~R, Seq[0]);  // AND_Gate
  and and_6 (and_6_out, R, Seq[0]);
  and and_7 (and_7_out, decoder_1_out10, Seq[5]);
  and and_8 (and_8_out, decoder_1_out7, Seq[5]);
  and and_9 (and_9_out, decoder_1_out14, Seq[6]);
  and and_10 (and_10_out, decoder_1_out12, Seq[6]);
  and and_11 (and_11_out, decoder_1_out13, Seq[6]);
  and and_12 (and_12_out, decoder_1_out9, Seq[5]);
  and and_13 (and_13_out, decoder_1_out8, Seq[5]);
  and and_14 (and_14_out, decoder_1_out14, Seq[5]);
  and and_15 (and_15_out, IR[12], and_1_out);
  and and_16 (and_16_out, Seq[2], ~R);  // AND_Gate
  and and_17 (and_17_out, R, Seq[1]);
  and and_18 (and_18_out, decoder_1_out9, Seq[6]);
  and and_19 (and_19_out, decoder_1_out14, Seq[7]);
  and and_20 (and_20_out, ~R, Seq[1]);  // AND_Gate
  and and_21 (and_21_out, ~decoder_1_out15, ~I0, ~I1, Seq[3]);  // AND_Gate
  and and_22 (and_22_out, ~decoder_1_out15, ~I0, I1, Seq[3]);  // AND_Gate
  and and_23 (and_23_out, ~decoder_1_out15, ~I0, I1, Seq[4]);  // AND_Gate
  or or_1 (or_1_out, and_2_out, and_4_out, and_3_out);
  or or_2 (or_2_out, and_5_out, and_6_out, and_7_out);
  or or_3 (or_3_out, and_8_out, and_9_out, and_10_out, and_11_out);
  or or_4 (or_4_out, and_12_out, and_13_out, and_14_out, and_15_out);
  or or_5 (or_5_out, and_17_out, and_18_out, and_19_out);
  or or_6 (or_6_out, and_20_out, and_21_out, and_22_out, and_23_out);
  and and_24 (and_24_out, ~or_6_out, ~or_5_out, ~and_16_out, ~or_4_out, ~or_3_out, ~or_2_out, ~or_1_out);  // AND_Gate
  Priority_Encoder priority_encoder_1 (
    .in0(and_24_out), .in1(or_1_out), .in2(or_2_out), .in3(or_3_out), .in4(or_4_out), .in5(and_16_out),
    .in6(or_5_out), .in7(or_6_out), .out({S2, S1, S0}));  // open: en_in, gs, en_out

  // Notes on the sheet:
  //   AR
  //   PC
  //   DR
  //   AC
  //   IR
  //   TR
  //   RAM
endmodule

module AR (
  input  [18:0] BUS_IN,
  input  LD,
  input  INR,
  input  CLR,
  output [18:0] BUS_OUT
);

  wire CLK_out;

  Clock CLK (.out(CLK_out));
  Counter #(.width(13), .max('h1fff)) counter_1 (
    .load(LD), .D(BUS_IN[12:0]), .count(INR), .Q(BUS_OUT[12:0]), .clk(CLK_out), .clr(CLR));  // open: carry

  assign BUS_OUT[18:13] = {6{1'b0}};
endmodule

module DR (
  input  [18:0] BUS_IN,
  input  INR,
  input  LD,
  input  CLR,
  output [18:0] BUS_OUT
);

  wire CLK_out;

  Clock CLK (.out(CLK_out));
  Counter #(.width(19), .max('h7ffff)) counter_1 (
    .load(LD), .D(BUS_IN), .count(INR), .Q(BUS_OUT), .clk(CLK_out), .clr(CLR));  // open: carry
endmodule

module PC (
  input  [18:0] BUS_IN,
  input  LD,
  input  INR,
  input  CLR,
  output [18:0] BUS_OUT
);

  wire CLK_out;

  Clock CLK (.out(CLK_out));
  Counter #(.width(13), .max('h1fff)) counter_1 (
    .load(LD), .D(BUS_IN[12:0]), .count(INR), .Q(BUS_OUT[12:0]), .clk(CLK_out), .clr(CLR));  // open: carry

  assign BUS_OUT[18:13] = {6{1'b0}};
endmodule

module IR (
  input  [18:0] Data_Bus_In,
  input  LD,
  input  INR,
  input  CLR,
  output [18:0] Bus_Out
);

  wire CLK_out;

  Clock CLK (.out(CLK_out));
  Counter #(.width(19), .max('h7ffff)) counter_1 (
    .load(LD), .D(Data_Bus_In), .count(INR), .Q(Bus_Out), .clk(CLK_out), .clr(CLR));  // open: carry
endmodule

module AC (
  input  [18:0] Data_Bus_In,
  input  LD,
  input  INR,
  input  CLR,
  output [18:0] Bus_Out
);

  wire CLK_out;

  Clock CLK (.out(CLK_out));
  Counter #(.width(19), .max('h7ffff)) counter_1 (
    .load(LD), .D(Data_Bus_In), .count(INR), .Q(Bus_Out), .clk(CLK_out), .clr(CLR));  // open: carry
endmodule

module TR (
  input  [18:0] Data_Bus_In,
  input  LD,
  input  INR,
  input  CLR,
  output [18:0] Bus_Out
);

  wire CLK_out;

  Clock CLK (.out(CLK_out));
  Counter #(.width(19), .max('h7ffff)) counter_1 (
    .load(LD), .D(Data_Bus_In), .count(INR), .Q(Bus_Out), .clk(CLK_out), .clr(CLR));  // open: carry
endmodule

module OUTR (
  input  [19:0] ALU_In,
  input  LD,
  output [7:0] Display_Unit
);

  wire CLk_out;

  Counter counter_1 (.load(LD), .D(ALU_In[7:0]), .count(1'b0), .Q(Display_Unit), .clk(CLk_out));  // open: carry, clr
  Clock CLk (.out(CLk_out));
endmodule

// 19-bit Common Bus
module BUS (
  input  S0,
  input  S1,
  input  S2,
  input  [18:0] AR,
  input  [18:0] PC,
  input  [18:0] DR,
  input  [18:0] AC,
  input  [18:0] IR,
  input  [18:0] TR,
  input  [18:0] RAM,
  output [18:0] out_11
);

  Multiplexer #(.select(3), .width(19)) multiplexer_1 (
    .in1(AR), .in2(PC), .in3(DR), .in4(AC), .in5(IR), .in6(TR), .in7(RAM), .out(out_11), .sel({S2, S1, S0}));  // open: in0, en

  // Other names for the same wires on the sheet: Selector[2:0] = {S2, S1, S0}
endmodule

module AR_Controller (
  input  [18:0] IR,
  input  [15:0] Seq,
  input  R,
  output LD,
  output INR,
  output CLR
);

  wire and_1_out, and_2_out, and_3_out, decoder_1_out0, decoder_1_out1, decoder_1_out2, decoder_1_out3,
       decoder_1_out4, decoder_1_out5, decoder_1_out6, decoder_1_out7, decoder_1_out8, decoder_1_out9,
       decoder_1_out10, decoder_1_out11, decoder_1_out12, decoder_1_out13, decoder_1_out14, decoder_1_out15;

  Decoder #(.select(4)) decoder_1 (
    .out0(decoder_1_out0), .out1(decoder_1_out1), .out2(decoder_1_out2), .out3(decoder_1_out3),
    .out4(decoder_1_out4), .out5(decoder_1_out5), .out6(decoder_1_out6), .out7(decoder_1_out7),
    .out8(decoder_1_out8), .out9(decoder_1_out9), .out10(decoder_1_out10), .out11(decoder_1_out11),
    .out12(decoder_1_out12), .out13(decoder_1_out13), .out14(decoder_1_out14), .out15(decoder_1_out15),
    .sel(IR[16:13]));  // open: en
  and and_1 (and_1_out, ~decoder_1_out15, IR[17], ~IR[18], Seq[3]);  // AND_Gate
  and and_2 (and_2_out, Seq[0], ~R);  // AND_Gate
  and and_3 (and_3_out, ~R, Seq[2]);  // AND_Gate
  and and_4 (INR, decoder_1_out10, Seq[5]);
  and and_5 (CLR, Seq[0], R);
  or or_1 (LD, and_1_out, and_2_out, and_3_out);

  // Other names for the same wires on the sheet: I1 = IR[17]; I0 = IR[18]
endmodule

module PC_Controller (
  input  [18:0] IR,
  input  [15:0] Seq,
  input  R,
  input  E,
  input  FGI,
  input  FGO,
  input  [19:0] AC,
  input  [19:0] DR,
  output LD,
  output INC,
  output CLR
);

  wire AC_t, and_3_out, and_4_out, and_5_out, and_6_out, and_7_out, and_8_out, and_9_out, and_10_out,
       and_11_out, and_12_out, and_13_out, and_14_out, and_15_out, and_16_out, and_17_out, decoder_1_out0,
       decoder_1_out1, decoder_1_out2, decoder_1_out3, decoder_1_out4, decoder_1_out5, decoder_1_out6,
       decoder_1_out7, decoder_1_out8, decoder_1_out9, decoder_1_out10, decoder_1_out11, decoder_1_out12,
       decoder_1_out13, decoder_1_out14, decoder_1_out15, DR_t, p, r_t;

  or or_1 (AC_t, AC[0], AC[1], AC[2], AC[3], AC[4], AC[5], AC[6], AC[7], AC[8], AC[9], AC[10], AC[11], AC[12], AC[13], AC[14], AC[15], AC[16], AC[17], AC[18], AC[19]);
  or or_2 (DR_t, DR[0], DR[1], DR[2], DR[3], DR[4], DR[5], DR[6], DR[7], DR[8], DR[9], DR[10], DR[11], DR[12], DR[13], DR[14], DR[15], DR[16], DR[17], DR[18], DR[19]);
  Decoder #(.select(4)) decoder_1 (
    .out0(decoder_1_out0), .out1(decoder_1_out1), .out2(decoder_1_out2), .out3(decoder_1_out3),
    .out4(decoder_1_out4), .out5(decoder_1_out5), .out6(decoder_1_out6), .out7(decoder_1_out7),
    .out8(decoder_1_out8), .out9(decoder_1_out9), .out10(decoder_1_out10), .out11(decoder_1_out11),
    .out12(decoder_1_out12), .out13(decoder_1_out13), .out14(decoder_1_out14), .out15(decoder_1_out15),
    .sel(IR[16:13]));  // open: en
  and and_1 (r_t, decoder_1_out15, ~IR[17], ~IR[18], Seq[3]);  // AND_Gate
  and and_2 (p, decoder_1_out15, IR[17], IR[18], Seq[3]);
  and and_3 (and_3_out, decoder_1_out11, Seq[5]);
  and and_4 (and_4_out, decoder_1_out10, Seq[6]);
  and and_5 (and_5_out, ~R, Seq[1]);  // AND_Gate
  and and_6 (and_6_out, R, Seq[2]);
  and and_7 (and_7_out, decoder_1_out9, ~AC_t, Seq[6]);  // AND_Gate
  and and_8 (and_8_out, decoder_1_out12, ~DR_t, Seq[6]);  // AND_Gate
  and and_9 (and_9_out, decoder_1_out13, ~DR_t, Seq[6]);  // AND_Gate
  and and_10 (and_10_out, r_t, ~AC[19], IR[4]);  // AND_Gate
  and and_11 (and_11_out, r_t, AC[19], IR[5]);
  and and_12 (and_12_out, r_t, ~AC_t, IR[2]);  // AND_Gate
  and and_13 (and_13_out, r_t, ~E, IR[3]);  // AND_Gate
  and and_14 (and_14_out, p, FGI, IR[9]);
  and and_15 (and_15_out, p, ~FGI, IR[8]);  // AND_Gate
  and and_16 (and_16_out, p, FGO, IR[7]);
  and and_17 (and_17_out, p, ~FGO, IR[6]);  // AND_Gate
  and and_18 (CLR, R, Seq[1]);
  or or_3 (LD, and_3_out, and_4_out);
  or or_4 (INC, and_5_out, and_6_out, and_7_out, and_8_out, and_9_out, and_10_out, and_11_out, and_12_out, and_13_out, and_14_out, and_15_out, and_16_out, and_17_out);

  // Other names for the same wires on the sheet: AC_19 = AC[19]; I1 = IR[17]; I0 = IR[18]
endmodule

module TR_Controller (
  input  [18:0] IR,
  input  [15:0] Seq,
  input  R,
  output LD
);

  wire and_1_out, and_2_out, and_3_out, decoder_1_out0, decoder_1_out1, decoder_1_out2, decoder_1_out3,
       decoder_1_out4, decoder_1_out5, decoder_1_out6, decoder_1_out7, decoder_1_out8, decoder_1_out9,
       decoder_1_out10, decoder_1_out11, decoder_1_out12, decoder_1_out13, decoder_1_out14, decoder_1_out15;

  Decoder #(.select(4)) decoder_1 (
    .out0(decoder_1_out0), .out1(decoder_1_out1), .out2(decoder_1_out2), .out3(decoder_1_out3),
    .out4(decoder_1_out4), .out5(decoder_1_out5), .out6(decoder_1_out6), .out7(decoder_1_out7),
    .out8(decoder_1_out8), .out9(decoder_1_out9), .out10(decoder_1_out10), .out11(decoder_1_out11),
    .out12(decoder_1_out12), .out13(decoder_1_out13), .out14(decoder_1_out14), .out15(decoder_1_out15),
    .sel(IR[16:13]));  // open: en
  and and_1 (and_1_out, R, Seq[0]);
  and and_2 (and_2_out, decoder_1_out9, Seq[5]);
  and and_3 (and_3_out, Seq[5], decoder_1_out14);
  or or_1 (LD, and_1_out, and_2_out, and_3_out);
endmodule

module SC_Controller (
  input  [18:0] IR,
  input  [15:0] Seq,
  input  R,
  input  S,
  output LD,
  output INC
);

  wire and_1_out, and_2_out, and_3_out, and_4_out, and_5_out, and_6_out, and_7_out, and_8_out, and_9_out,
       and_10_out, and_11_out, and_12_out, and_13_out, and_14_out, and_15_out, and_16_out, decoder_1_out0,
       decoder_1_out1, decoder_1_out2, decoder_1_out3, decoder_1_out4, decoder_1_out5, decoder_1_out6,
       decoder_1_out7, decoder_1_out8, decoder_1_out9, decoder_1_out10, decoder_1_out11, decoder_1_out12,
       decoder_1_out13, decoder_1_out14, decoder_1_out15, or_1_out, p, r_t;

  Decoder #(.select(4)) decoder_1 (
    .out0(decoder_1_out0), .out1(decoder_1_out1), .out2(decoder_1_out2), .out3(decoder_1_out3),
    .out4(decoder_1_out4), .out5(decoder_1_out5), .out6(decoder_1_out6), .out7(decoder_1_out7),
    .out8(decoder_1_out8), .out9(decoder_1_out9), .out10(decoder_1_out10), .out11(decoder_1_out11),
    .out12(decoder_1_out12), .out13(decoder_1_out13), .out14(decoder_1_out14), .out15(decoder_1_out15),
    .sel(IR[16:13]));  // open: en
  and u_r (r_t, decoder_1_out15, ~IR[17], ~IR[18], Seq[3]);  // AND_Gate
  and u_p (p, decoder_1_out15, IR[17], IR[18], Seq[3]);
  and and_1 (and_1_out, R, Seq[2]);
  and and_2 (and_2_out, decoder_1_out5, Seq[5]);
  and and_3 (and_3_out, decoder_1_out4, Seq[5]);
  and and_4 (and_4_out, decoder_1_out6, Seq[5]);
  and and_5 (and_5_out, decoder_1_out3, Seq[5]);
  and and_6 (and_6_out, decoder_1_out2, Seq[5]);
  and and_7 (and_7_out, decoder_1_out0, Seq[5]);
  and and_8 (and_8_out, decoder_1_out1, Seq[5]);
  and and_9 (and_9_out, decoder_1_out7, Seq[5]);
  and and_10 (and_10_out, decoder_1_out8, Seq[5]);
  and and_11 (and_11_out, decoder_1_out9, Seq[6]);
  and and_12 (and_12_out, decoder_1_out10, Seq[6]);
  and and_13 (and_13_out, decoder_1_out12, Seq[6]);
  and and_14 (and_14_out, decoder_1_out13, Seq[6]);
  and and_15 (and_15_out, decoder_1_out11, Seq[5]);
  and and_16 (and_16_out, decoder_1_out14, Seq[7]);
  or or_1 (or_1_out, r_t, p, and_1_out, and_2_out, and_3_out, and_4_out, and_5_out, and_6_out, and_7_out, and_8_out, and_9_out, and_10_out, and_11_out, and_12_out, and_13_out, and_14_out, and_15_out, and_16_out);
  and and_17 (LD, or_1_out, S);
  and and_18 (INC, ~or_1_out, S);  // AND_Gate

  // Other names for the same wires on the sheet: I1 = IR[17]; I0 = IR[18]
endmodule

module IR_Controller (
  input  [18:0] IR,
  input  [15:0] Seq,
  input  R,
  output LD
);

  wire decoder_1_out0, decoder_1_out1, decoder_1_out2, decoder_1_out3, decoder_1_out4, decoder_1_out5,
       decoder_1_out6, decoder_1_out7, decoder_1_out8, decoder_1_out9, decoder_1_out10, decoder_1_out11,
       decoder_1_out12, decoder_1_out13, decoder_1_out14;

  Decoder #(.select(4)) decoder_1 (
    .out0(decoder_1_out0), .out1(decoder_1_out1), .out2(decoder_1_out2), .out3(decoder_1_out3),
    .out4(decoder_1_out4), .out5(decoder_1_out5), .out6(decoder_1_out6), .out7(decoder_1_out7),
    .out8(decoder_1_out8), .out9(decoder_1_out9), .out10(decoder_1_out10), .out11(decoder_1_out11),
    .out12(decoder_1_out12), .out13(decoder_1_out13), .out14(decoder_1_out14), .sel(IR[16:13]));  // open: out15, en
  and and_1 (LD, ~R, Seq[1]);  // AND_Gate
endmodule

module SC (
  input  Clear,
  input  Load,
  input  INC,
  input  CLK,
  output A,
  output A_2,
  output A_3,
  output A_4,
  output A_5,
  output A_6,
  output A_7,
  output A_8,
  output C_out
);

  wire and_1_out, and_2_out, and_3_out, and_4_out, and_5_out, and_6_out, and_7_out, and_8_out, and_9_out,
       and_10_out, and_11_out, and_12_out, and_13_out, and_14_out, and_15_out, and_16_out, and_18_out,
       and_19_out, and_21_out, and_22_out, and_24_out, and_25_out, or_1_out, or_2_out, or_3_out, or_4_out,
       or_5_out, or_6_out, or_7_out, or_8_out, or_9_out, or_10_out, or_11_out, or_12_out, or_13_out,
       or_14_out, or_15_out, or_16_out, undriven, undriven_2, undriven_3, undriven_4, undriven_5, undriven_6,
       undriven_7, undriven_8;

  and and_1 (and_1_out, ~Clear, Load);  // AND_Gate
  and and_2 (and_2_out, ~Clear, ~Load, INC);  // AND_Gate
  and and_3 (and_3_out, and_1_out, undriven);
  and and_4 (and_4_out, and_1_out, ~undriven);  // AND_Gate
  and and_5 (and_5_out, and_2_out, A);
  and and_6 (and_6_out, and_1_out, undriven_2);
  and and_7 (and_7_out, and_1_out, ~undriven_2);  // AND_Gate
  and and_8 (and_8_out, and_5_out, A_2);
  and and_9 (and_9_out, and_1_out, undriven_3);
  and and_10 (and_10_out, and_1_out, ~undriven_3);  // AND_Gate
  and and_11 (and_11_out, and_8_out, A_3);
  and and_12 (and_12_out, and_1_out, undriven_4);
  and and_13 (and_13_out, and_1_out, ~undriven_4);  // AND_Gate
  and and_14 (and_14_out, and_11_out, A_4);
  and and_15 (and_15_out, and_1_out, undriven_5);
  and and_16 (and_16_out, and_1_out, ~undriven_5);  // AND_Gate
  and and_17 (Clear, and_14_out, A_5);
  and and_18 (and_18_out, and_1_out, undriven_6);
  and and_19 (and_19_out, and_1_out, ~undriven_6);  // AND_Gate
  and and_20 (Clear, Clear, A_6);
  and and_21 (and_21_out, and_1_out, undriven_7);
  and and_22 (and_22_out, and_1_out, ~undriven_7);  // AND_Gate
  and and_23 (Clear, Clear, A_7);
  and and_24 (and_24_out, and_1_out, undriven_8);
  and and_25 (and_25_out, and_1_out, ~undriven_8);  // AND_Gate
  and and_26 (C_out, Clear, A_8);
  or or_1 (or_1_out, and_2_out, and_3_out);
  or or_2 (or_2_out, Clear, and_2_out, and_4_out);
  or or_3 (or_3_out, and_5_out, and_6_out);
  or or_4 (or_4_out, Clear, and_5_out, and_7_out);
  or or_5 (or_5_out, and_8_out, and_9_out);
  or or_6 (or_6_out, Clear, and_8_out, and_10_out);
  or or_7 (or_7_out, and_11_out, and_12_out);
  or or_8 (or_8_out, Clear, and_11_out, and_13_out);
  or or_9 (or_9_out, and_14_out, and_15_out);
  or or_10 (or_10_out, Clear, and_14_out, and_16_out);
  or or_11 (or_11_out, Clear, and_18_out);
  or or_12 (or_12_out, Clear, Clear, and_19_out);
  or or_13 (or_13_out, Clear, and_21_out);
  or or_14 (or_14_out, Clear, Clear, and_22_out);
  or or_15 (or_15_out, Clear, and_24_out);
  or or_16 (or_16_out, Clear, Clear, and_25_out);
  J_K_Flip_Flop j_k_ff_1 (.J(or_1_out), .clk(CLK), .K(or_2_out), .Q(A));  // open: Qn, preset, en, reset
  J_K_Flip_Flop j_k_ff_2 (.J(or_3_out), .clk(CLK), .K(or_4_out), .Q(A_2));  // open: Qn, preset, en, reset
  J_K_Flip_Flop j_k_ff_3 (.J(or_5_out), .clk(CLK), .K(or_6_out), .Q(A_3));  // open: Qn, preset, en, reset
  J_K_Flip_Flop j_k_ff_4 (.J(or_7_out), .clk(CLK), .K(or_8_out), .Q(A_4));  // open: Qn, preset, en, reset
  J_K_Flip_Flop j_k_ff_5 (.J(or_9_out), .clk(CLK), .K(or_10_out), .Q(A_5));  // open: Qn, preset, en, reset
  J_K_Flip_Flop j_k_ff_6 (.J(or_11_out), .clk(CLK), .K(or_12_out), .Q(A_6));  // open: Qn, preset, en, reset
  J_K_Flip_Flop j_k_ff_7 (.J(or_13_out), .clk(CLK), .K(or_14_out), .Q(A_7));  // open: Qn, preset, en, reset
  J_K_Flip_Flop j_k_ff_8 (.J(or_15_out), .clk(CLK), .K(or_16_out), .Q(A_8));  // open: Qn, preset, en, reset
endmodule

module DR_Controller (
  input  [18:0] IR,
  input  [15:0] Seq,
  input  R,
  output LD,
  output INC
);

  wire and_1_out, and_2_out, and_3_out, and_4_out, and_5_out, and_6_out, and_7_out, decoder_1_out0,
       decoder_1_out1, decoder_1_out2, decoder_1_out3, decoder_1_out4, decoder_1_out5, decoder_1_out6,
       decoder_1_out7, decoder_1_out8, decoder_1_out9, decoder_1_out10, decoder_1_out11, decoder_1_out12,
       decoder_1_out13, decoder_1_out14, decoder_1_out15;

  Decoder #(.select(4)) decoder_1 (
    .out0(decoder_1_out0), .out1(decoder_1_out1), .out2(decoder_1_out2), .out3(decoder_1_out3),
    .out4(decoder_1_out4), .out5(decoder_1_out5), .out6(decoder_1_out6), .out7(decoder_1_out7),
    .out8(decoder_1_out8), .out9(decoder_1_out9), .out10(decoder_1_out10), .out11(decoder_1_out11),
    .out12(decoder_1_out12), .out13(decoder_1_out13), .out14(decoder_1_out14), .out15(decoder_1_out15),
    .sel(IR[16:13]));  // open: en
  and and_1 (and_1_out, decoder_1_out14, Seq[7]);
  and and_2 (and_2_out, decoder_1_out12, Seq[5]);
  and and_3 (and_3_out, Seq[3], ~decoder_1_out15, ~IR[18], ~IR[17]);  // AND_Gate
  and and_4 (and_4_out, Seq[4], ~decoder_1_out15, ~IR[18], IR[17]);  // AND_Gate
  and and_5 (and_5_out, Seq[3], ~decoder_1_out15, IR[18], ~IR[17]);  // AND_Gate
  and and_6 (and_6_out, decoder_1_out13, Seq[5]);
  and and_7 (and_7_out, decoder_1_out12, Seq[5]);
  or or_1 (INC, and_6_out, and_7_out);
  or or_2 (LD, and_1_out, and_2_out, and_3_out, and_4_out, and_5_out);

  // Other names for the same wires on the sheet: I1 = IR[17]; I0 = IR[18]
endmodule

module IEN_Controller (
  input  [18:0] IR,
  input  [15:0] Seq,
  input  CLK,
  input  R,
  output Output
);

  wire and_1_out, and_2_out, and_3_out, and_4_out, and_5_out, decoder_1_out0, decoder_1_out1, decoder_1_out2,
       decoder_1_out3, decoder_1_out4, decoder_1_out5, decoder_1_out6, decoder_1_out7, decoder_1_out8,
       decoder_1_out9, decoder_1_out10, decoder_1_out11, decoder_1_out12, decoder_1_out13, decoder_1_out14,
       decoder_1_out15, or_1_out;

  Decoder #(.select(4)) decoder_1 (
    .out0(decoder_1_out0), .out1(decoder_1_out1), .out2(decoder_1_out2), .out3(decoder_1_out3),
    .out4(decoder_1_out4), .out5(decoder_1_out5), .out6(decoder_1_out6), .out7(decoder_1_out7),
    .out8(decoder_1_out8), .out9(decoder_1_out9), .out10(decoder_1_out10), .out11(decoder_1_out11),
    .out12(decoder_1_out12), .out13(decoder_1_out13), .out14(decoder_1_out14), .out15(decoder_1_out15),
    .sel(IR[16:13]));  // open: en
  and and_1 (and_1_out, decoder_1_out15, IR[18], IR[18], Seq[3]);
  and and_2 (and_2_out, decoder_1_out15, IR[18], IR[18], Seq[3]);
  and and_3 (and_3_out, and_1_out, IR[11]);
  and and_4 (and_4_out, and_2_out, IR[10]);
  and and_5 (and_5_out, R, Seq[2]);
  or or_1 (or_1_out, and_4_out, and_5_out);
  J_K_Flip_Flop j_k_ff_1 (.J(and_3_out), .clk(CLK), .K(or_1_out), .Q(Output));  // open: Qn, preset, en, reset

  assign IR[17] = IR[18];

  // Other names for the same wires on the sheet: I1 = IR[18]; IO = IR[18]
endmodule

module FGO_Controller (
  input  [18:0] IR,
  input  [15:0] Seq,
  input  CLK,
  output Output
);

  wire and_1_out, decoder_1_out0, decoder_1_out1, decoder_1_out2, decoder_1_out3, decoder_1_out4,
       decoder_1_out5, decoder_1_out6, decoder_1_out7, decoder_1_out8, decoder_1_out9, decoder_1_out10,
       decoder_1_out11, decoder_1_out12, decoder_1_out13, decoder_1_out14, decoder_1_out15, p_out;

  Decoder #(.select(4)) decoder_1 (
    .out0(decoder_1_out0), .out1(decoder_1_out1), .out2(decoder_1_out2), .out3(decoder_1_out3),
    .out4(decoder_1_out4), .out5(decoder_1_out5), .out6(decoder_1_out6), .out7(decoder_1_out7),
    .out8(decoder_1_out8), .out9(decoder_1_out9), .out10(decoder_1_out10), .out11(decoder_1_out11),
    .out12(decoder_1_out12), .out13(decoder_1_out13), .out14(decoder_1_out14), .out15(decoder_1_out15),
    .sel(IR[16:13]));  // open: en
  and p (p_out, decoder_1_out15, IR[18], IR[17], Seq[3]);
  and and_1 (and_1_out, p_out, IR[12]);
  J_K_Flip_Flop j_k_ff_1 (.J(1'b0), .clk(CLK), .K(and_1_out), .Q(Output));  // open: Qn, preset, en, reset

  // Other names for the same wires on the sheet: I1 = IR[17]; I0 = IR[18]
endmodule

module FGI_Controller (
  input  [18:0] IR,
  input  [15:0] Seq,
  input  CLK,
  output Output
);

  wire and_1_out, decoder_1_out0, decoder_1_out1, decoder_1_out2, decoder_1_out3, decoder_1_out4,
       decoder_1_out5, decoder_1_out6, decoder_1_out7, decoder_1_out8, decoder_1_out9, decoder_1_out10,
       decoder_1_out11, decoder_1_out12, decoder_1_out13, decoder_1_out14, decoder_1_out15, p_out;

  Decoder #(.select(4)) decoder_1 (
    .out0(decoder_1_out0), .out1(decoder_1_out1), .out2(decoder_1_out2), .out3(decoder_1_out3),
    .out4(decoder_1_out4), .out5(decoder_1_out5), .out6(decoder_1_out6), .out7(decoder_1_out7),
    .out8(decoder_1_out8), .out9(decoder_1_out9), .out10(decoder_1_out10), .out11(decoder_1_out11),
    .out12(decoder_1_out12), .out13(decoder_1_out13), .out14(decoder_1_out14), .out15(decoder_1_out15),
    .sel(IR[16:13]));  // open: en
  and p (p_out, decoder_1_out15, IR[18], IR[17], Seq[3]);
  and and_1 (and_1_out, p_out, IR[5]);
  J_K_Flip_Flop j_k_ff_1 (.J(1'b0), .clk(CLK), .K(and_1_out), .Q(Output));  // open: Qn, preset, en, reset

  // Other names for the same wires on the sheet: I1 = IR[17]; I0 = IR[18]
endmodule

module R_Controller (
  input  [15:0] Seq,
  input  IEN,
  input  FGI,
  input  FGO,
  input  CLK,
  output Output
);

  wire and_1_out, and_2_out, or_1_out;

  or or_1 (or_1_out, FGI, FGO);
  and and_1 (and_1_out, ~Seq[0], ~Seq[1], ~Seq[2], IEN, or_1_out);  // AND_Gate
  and and_2 (and_2_out, Seq[2], Output);
  J_K_Flip_Flop j_k_ff_1 (.J(and_1_out), .clk(CLK), .K(and_2_out), .Q(Output));  // open: Qn, preset, en, reset
endmodule

module OUTR_Controller (
  input  [18:0] IR,
  input  [15:0] Seq,
  input  R,
  output LD
);

  wire decoder_1_out0, decoder_1_out1, decoder_1_out2, decoder_1_out3, decoder_1_out4, decoder_1_out5,
       decoder_1_out6, decoder_1_out7, decoder_1_out8, decoder_1_out9, decoder_1_out10, decoder_1_out11,
       decoder_1_out12, decoder_1_out13, decoder_1_out14, decoder_1_out15, p_out;

  Decoder #(.select(4)) decoder_1 (
    .out0(decoder_1_out0), .out1(decoder_1_out1), .out2(decoder_1_out2), .out3(decoder_1_out3),
    .out4(decoder_1_out4), .out5(decoder_1_out5), .out6(decoder_1_out6), .out7(decoder_1_out7),
    .out8(decoder_1_out8), .out9(decoder_1_out9), .out10(decoder_1_out10), .out11(decoder_1_out11),
    .out12(decoder_1_out12), .out13(decoder_1_out13), .out14(decoder_1_out14), .out15(decoder_1_out15),
    .sel(IR[16:13]));  // open: en
  and p (p_out, decoder_1_out15, IR[17], IR[18], Seq[3]);
  and and_1 (LD, p_out, IR[11]);

  // Other names for the same wires on the sheet: I1 = IR[17]; I0 = IR[18]
endmodule

module Memory_Controller (
  input  [18:0] IR,
  input  [15:0] Seq,
  input  R,
  output Read,
  output Write
);

  wire and_1_out, and_2_out, and_3_out, and_4_out, and_5_out, and_6_out, and_7_out, and_8_out, and_9_out,
       decoder_1_out0, decoder_1_out1, decoder_1_out2, decoder_1_out3, decoder_1_out4, decoder_1_out5,
       decoder_1_out6, decoder_1_out7, decoder_1_out8, decoder_1_out9, decoder_1_out10, decoder_1_out11,
       decoder_1_out12, decoder_1_out13, decoder_1_out14, decoder_1_out15;

  Decoder #(.select(4)) decoder_1 (
    .out0(decoder_1_out0), .out1(decoder_1_out1), .out2(decoder_1_out2), .out3(decoder_1_out3),
    .out4(decoder_1_out4), .out5(decoder_1_out5), .out6(decoder_1_out6), .out7(decoder_1_out7),
    .out8(decoder_1_out8), .out9(decoder_1_out9), .out10(decoder_1_out10), .out11(decoder_1_out11),
    .out12(decoder_1_out12), .out13(decoder_1_out13), .out14(decoder_1_out14), .out15(decoder_1_out15),
    .sel(IR[16:13]));  // open: en
  and and_1 (and_1_out, R, Seq[1]);
  and and_2 (and_2_out, decoder_1_out8, Seq[5]);
  and and_3 (and_3_out, decoder_1_out10, Seq[5]);
  and and_4 (and_4_out, decoder_1_out12, Seq[6]);
  and and_5 (and_5_out, decoder_1_out13, Seq[6]);
  and and_6 (and_6_out, ~R, Seq[1]);  // AND_Gate
  and and_7 (and_7_out, ~decoder_1_out15, ~IR[17], ~IR[18], Seq[3]);  // AND_Gate
  and and_8 (and_8_out, IR[17], ~decoder_1_out15, ~IR[18], Seq[3]);  // AND_Gate
  and and_9 (and_9_out, ~decoder_1_out15, ~IR[18], IR[17], Seq[4]);  // AND_Gate
  or or_1 (Read, and_6_out, and_7_out, and_8_out, and_9_out);
  or or_2 (Write, and_1_out, and_2_out, and_3_out, and_4_out, and_5_out);

  // Other names for the same wires on the sheet: I1 = IR[17]; I0 = IR[18]
endmodule

module Bus_Controller (
  input  [18:0] IR,
  input  [15:0] Seq,
  input  R,
  input  I0,
  input  I1,
  output S0,
  output S1,
  output S2
);

  wire and_1_out, and_2_out, and_3_out, and_4_out, and_5_out, and_6_out, and_7_out, and_8_out, and_9_out,
       and_10_out, and_11_out, and_12_out, and_13_out, and_14_out, and_15_out, and_16_out, and_17_out,
       and_18_out, and_19_out, and_20_out, and_21_out, and_22_out, and_23_out, and_24_out, decoder_1_out0,
       decoder_1_out1, decoder_1_out2, decoder_1_out3, decoder_1_out4, decoder_1_out5, decoder_1_out6,
       decoder_1_out7, decoder_1_out8, decoder_1_out9, decoder_1_out10, decoder_1_out11, decoder_1_out12,
       decoder_1_out13, decoder_1_out14, decoder_1_out15, or_1_out, or_2_out, or_3_out, or_4_out, or_5_out,
       or_6_out;

  Decoder #(.select(4)) decoder_1 (
    .out0(decoder_1_out0), .out1(decoder_1_out1), .out2(decoder_1_out2), .out3(decoder_1_out3),
    .out4(decoder_1_out4), .out5(decoder_1_out5), .out6(decoder_1_out6), .out7(decoder_1_out7),
    .out8(decoder_1_out8), .out9(decoder_1_out9), .out10(decoder_1_out10), .out11(decoder_1_out11),
    .out12(decoder_1_out12), .out13(decoder_1_out13), .out14(decoder_1_out14), .out15(decoder_1_out15),
    .sel(IR[16:13]));  // open: en
  and and_1 (and_1_out, decoder_1_out15, Seq[3], I0, I1);
  and and_2 (and_2_out, decoder_1_out10, Seq[6]);
  and and_3 (and_3_out, Seq[5], decoder_1_out11);
  and and_4 (and_4_out, ~decoder_1_out15, Seq[3], I0, ~I1);  // AND_Gate
  and and_5 (and_5_out, ~R, Seq[0]);  // AND_Gate
  and and_6 (and_6_out, R, Seq[0]);
  and and_7 (and_7_out, decoder_1_out10, Seq[5]);
  and and_8 (and_8_out, decoder_1_out7, Seq[5]);
  and and_9 (and_9_out, decoder_1_out14, Seq[6]);
  and and_10 (and_10_out, decoder_1_out12, Seq[6]);
  and and_11 (and_11_out, decoder_1_out13, Seq[6]);
  and and_12 (and_12_out, decoder_1_out9, Seq[5]);
  and and_13 (and_13_out, decoder_1_out8, Seq[5]);
  and and_14 (and_14_out, decoder_1_out14, Seq[5]);
  and and_15 (and_15_out, IR[11], and_1_out);
  and and_16 (and_16_out, Seq[2], ~R);  // AND_Gate
  and and_17 (and_17_out, R, Seq[1]);
  and and_18 (and_18_out, decoder_1_out9, Seq[6]);
  and and_19 (and_19_out, decoder_1_out14, Seq[7]);
  and and_20 (and_20_out, ~R, Seq[1]);  // AND_Gate
  and and_21 (and_21_out, ~decoder_1_out15, ~I0, ~I1, Seq[3]);  // AND_Gate
  and and_22 (and_22_out, ~decoder_1_out15, ~I0, I1, Seq[3]);  // AND_Gate
  and and_23 (and_23_out, ~decoder_1_out15, ~I0, I1, Seq[4]);  // AND_Gate
  or or_1 (or_1_out, and_2_out, and_4_out, and_3_out);
  or or_2 (or_2_out, and_5_out, and_6_out, and_7_out);
  or or_3 (or_3_out, and_8_out, and_9_out, and_10_out, and_11_out);
  or or_4 (or_4_out, and_12_out, and_13_out, and_14_out, and_15_out);
  or or_5 (or_5_out, and_17_out, and_18_out, and_19_out);
  or or_6 (or_6_out, and_20_out, and_21_out, and_22_out, and_23_out);
  and and_24 (and_24_out, ~or_6_out, ~or_5_out, ~and_16_out, ~or_4_out, ~or_3_out, ~or_2_out, ~or_1_out);  // AND_Gate
  Priority_Encoder priority_encoder_1 (
    .in0(and_24_out), .in1(or_1_out), .in2(or_2_out), .in3(or_3_out), .in4(or_4_out), .in5(and_16_out),
    .in6(or_5_out), .in7(or_6_out), .out({S2, S1, S0}));  // open: en_in, gs, en_out

  // Other names for the same wires on the sheet: IR12 = IR[11]

  // Notes on the sheet:
  //   IR
  //   AR
  //   PC
  //   DR
  //   AC
  //   TR
  //   RAM
endmodule

module E_Controller (
  input  [18:0] IR,
  input  [19:0] AC,
  input  [15:0] Seq,
  input  R,
  input  in_5,
  input  Cout,
  output Output
);

  wire and_1_out, and_2_out, and_3_out, and_4_out, and_5_out, and_6_out, and_7_out, and_8_out, and_9_out,
       decoder_1_out0, decoder_1_out1, decoder_1_out2, decoder_1_out3, decoder_1_out4, decoder_1_out5,
       decoder_1_out6, decoder_1_out7, decoder_1_out8, decoder_1_out9, decoder_1_out10, decoder_1_out11,
       decoder_1_out12, decoder_1_out13, decoder_1_out14, decoder_1_out15, or_1_out, or_2_out, r_out;

  Decoder #(.select(4)) decoder_1 (
    .out0(decoder_1_out0), .out1(decoder_1_out1), .out2(decoder_1_out2), .out3(decoder_1_out3),
    .out4(decoder_1_out4), .out5(decoder_1_out5), .out6(decoder_1_out6), .out7(decoder_1_out7),
    .out8(decoder_1_out8), .out9(decoder_1_out9), .out10(decoder_1_out10), .out11(decoder_1_out11),
    .out12(decoder_1_out12), .out13(decoder_1_out13), .out14(decoder_1_out14), .out15(decoder_1_out15),
    .sel(IR[16:13]));  // open: en
  and u_r (r_out, decoder_1_out15, ~IR[18], ~IR[17], Seq[3]);  // AND_Gate
  and and_1 (and_1_out, decoder_1_out0, Cout, Seq[5]);
  and and_2 (and_2_out, r_out, IR[8], AC[0]);
  and and_3 (and_3_out, r_out, IR[9], AC[19]);
  and and_4 (and_4_out, r_out, IR[6]);
  and and_5 (and_5_out, r_out, IR[10]);
  and and_6 (and_6_out, r_out, IR[11]);
  and and_7 (and_7_out, ~Cout, Seq[5], decoder_1_out0);  // AND_Gate
  and and_8 (and_8_out, r_out, IR[8], ~AC[0]);  // AND_Gate
  and and_9 (and_9_out, r_out, IR[9], ~AC[19]);  // AND_Gate
  or or_1 (or_1_out, and_1_out, and_2_out, and_3_out, and_4_out);
  or or_2 (or_2_out, and_5_out, and_6_out, and_7_out, and_8_out, and_9_out);
  J_K_Flip_Flop j_k_ff_1 (.J(or_1_out), .clk(in_5), .K(or_2_out), .Q(Output));  // open: Qn, preset, en, reset

  // Other names for the same wires on the sheet: I1 = IR[17]; I0 = IR[18]
endmodule

module S_Controller (
  input  [18:0] IR,
  input  [15:0] Seq,
  input  CLK,
  input  R,
  output Output
);

  wire and_1_out, and_2_out, decoder_1_out0, decoder_1_out1, decoder_1_out2, decoder_1_out3, decoder_1_out4,
       decoder_1_out5, decoder_1_out6, decoder_1_out7, decoder_1_out8, decoder_1_out9, decoder_1_out10,
       decoder_1_out11, decoder_1_out12, decoder_1_out13, decoder_1_out14, decoder_1_out15;

  Decoder #(.select(4)) decoder_1 (
    .out0(decoder_1_out0), .out1(decoder_1_out1), .out2(decoder_1_out2), .out3(decoder_1_out3),
    .out4(decoder_1_out4), .out5(decoder_1_out5), .out6(decoder_1_out6), .out7(decoder_1_out7),
    .out8(decoder_1_out8), .out9(decoder_1_out9), .out10(decoder_1_out10), .out11(decoder_1_out11),
    .out12(decoder_1_out12), .out13(decoder_1_out13), .out14(decoder_1_out14), .out15(decoder_1_out15),
    .sel(IR[16:13]));  // open: en
  and and_1 (and_1_out, decoder_1_out15, ~IR[18], ~IR[18], Seq[3]);  // AND_Gate
  and and_2 (and_2_out, and_1_out, IR[1]);
  J_K_Flip_Flop j_k_ff_1 (.J(1'b0), .clk(CLK), .K(1'b0), .Qn(Output), .preset(and_2_out));  // open: Q, en, reset

  // Other names for the same wires on the sheet: I0 = IR[18]; I1 = IR[18]
endmodule
